# Fritzing sketch DoorLaser (saved by Fritzing 0.9.3b)
breadboards: 1

parts:
  Bauteil1 = ESP32 Module Testbed  # not connected
  Power_plug1 = Power plug
  KY-008_Laserdiode1 = Laser [part_number=1219301 package=keys]
  Q1 = LTR-301 [package=ltr-301]
  R1 = Resistor [tolerance=±5% resistance=220 package="0402 [SMD]"]
  S1 = SWITCH-MOMENTARY-2 [package=reed_switch_plastic]
  R2 = Resistor [tolerance=±5% resistance=220 package="0402 [SMD]"]

nets:
  N1: Power_plug1.GND, KY-008_Laserdiode1.connector2pin, R1.Pin_1, R2.Pin_0
  N2: Power_plug1.VCC, KY-008_Laserdiode1.connector1pin, Q1.E, S1.2
  N3: Q1.C, R1.Pin_0
  N4: S1.1, R2.Pin_1

notes:
  5V Power Supply
  (Note: the second GND is actually 5V)

custom parts:
  ESP32 Module Testbed: The ESP32 Module Testbed is a breadboard compatible breakout board for the ESP-WROOM-03 ESP32 module. The ESP32 is a WiFi and Bluetooth-enabled 32-bit, dual-core microcontroller.
  Laser: KEYES KY-008 650nm Laser Transmitter Module
