# Fritzing sketch SensorStation (saved by Fritzing 0.9.3b)
breadboards: 1

parts:
  Bauteil1 = ESP32 Module Testbed
  RHT1 = Humidity and Temperature Sensor RHT03
  R1 = Resistor [tolerance=±5% resistance=220 package="2512 [SMD]"]

nets:
  N1: Bauteil1.GND, RHT1.GND_2
  3V3: Bauteil1.3V3, RHT1.Vcc, R1.Pin_0
  N2: RHT1.Data-signal, R1.Pin_1

custom parts:
  ESP32 Module Testbed: The ESP32 Module Testbed is a breadboard compatible breakout board for the ESP-WROOM-03 ESP32 module. The ESP32 is a WiFi and Bluetooth-enabled 32-bit, dual-core microcontroller.
